# Fritzing sketch carBody (saved by Fritzing 0.9.6b)

parts:
  L298N1 = L298N DC motor driver
  M1 = DOIT Esp32 DevKit v1 (30 pins long, 11 pins width) [part_number=ESP32S-PIN30]
  M2 = gear-motor
  L298N2 = L298N DC motor driver
  M3 = gear-motor
  M4 = gear-motor
  M5 = gear-motor
  BAT1 = BC9VPC [package=bc9vpc]

nets:
  N1: L298N1.OUT1, M5.pin_2
  N2: L298N1.OUT2, M5.pin_1
  N3: L298N1.OUT3, M4.pin_1
  N4: L298N1.OUT4, M4.pin_2
  12V: L298N1.12V, M1.VIN, L298N2.12V, BAT1.V+
  GND: L298N1.GND, M1.GND, L298N2.GND, BAT1.V-
  N5: L298N1.ENA, M1.D25
  N6: L298N1.ENB, M1.D13
  N7: L298N1.IN1, M1.D26
  N8: L298N1.IN2, M1.D27
  N9: L298N1.IN3, M1.D14
  N10: L298N1.IN4, M1.D12
  N11: M1.D15, L298N2.ENA
  N12: M1.D2, L298N2.IN1
  N13: M1.D4, L298N2.IN2
  N14: M1.RX2, L298N2.IN3
  N15: M1.TX2, L298N2.IN4
  N16: M1.D5, L298N2.ENB
  N17: M2.pin_1, L298N2.OUT3
  N18: M2.pin_2, L298N2.OUT4
  N19: L298N2.OUT1, M3.pin_2
  N20: L298N2.OUT2, M3.pin_1

custom parts:
  L298N DC motor driver: 2x DC motor driver with 78M05 positive voltage regulator (7..35 V) L298N: max 46 V, 2 A Set 5 V Enable jumper to enable 5 V regultor (needed for the L298N) and +5 V output at screw terminal or supply external +5 V at screw terminal Set ENA and/or ENB to +5 V to enable motor permanently or supply ENA and/or ENB with PWM signal IN1 and IN2 set rotation directory for motor A (OUT1/OUT2) IN2 and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
  DOIT Esp32 DevKit v1 (30 pins long, 11 pins width): The DOIT Esp32 DevKit v1 is one of the development board created by DOIT to evaluate the ESP-WROOM-32 module. It is based on the ESP32 microcontroller that boasts Wifi, Bluetooth, Ethernet and Low Power support all in a single chip. (vanepp) made breadboard work, adjusted pin numbering and labels and reduced size of schematic and cleaned up pcb. This chip is 30pins long (2 x15) and 11 pins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
