# Fritzing sketch joyControl (saved by Fritzing 0.9.6b)

parts:
  Mod1 = KY-023 Dual Axis Joystick Module [package="Breakout board"]
  M1 = DOIT Esp32 DevKit v1 (30 pins long, 11 pins width) [part_number=ESP32S-PIN30]
  BAT1 = BC9VPC [package=bc9vpc]

nets:
  GND: Mod1.GND, M1.GND, BAT1.V-
  +5V: Mod1.+5V, M1.3V3
  N1: Mod1.VRx, M1.D33
  N2: Mod1.VRy, M1.D32
  N3: Mod1.SW, M1.D13
  N4: M1.VIN, BAT1.V+

custom parts:
  KY-023 Dual Axis Joystick Module: KY-023 Dual-Axis Joystick Module.
  DOIT Esp32 DevKit v1 (30 pins long, 11 pins width): The DOIT Esp32 DevKit v1 is one of the development board created by DOIT to evaluate the ESP-WROOM-32 module. It is based on the ESP32 microcontroller that boasts Wifi, Bluetooth, Ethernet and Low Power support all in a single chip. (vanepp) made breadboard work, adjusted pin numbering and labels and reduced size of schematic and cleaned up pcb. This chip is 30pins long (2 x15) and 11 pins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
